// Logisim project 4bitANDer.circ as structural Verilog: 1 circuit, main circuit fourbitander
module fourbitander (
  input  a3,
  input  b3,
  input  a2,
  input  b2,
  input  a1,
  input  b1,
  input  a0,
  input  b0,
  output and3,
  output and2,
  output and1,
  output and0
);

  and and_1 (and3, a3, b3);
  and and_2 (and2, a2, b2);
  and and_3 (and1, a1, b1);
  and and_4 (and0, a0, b0);
endmodule
