// Logisim project 4bitORer.circ as structural Verilog: 1 circuit, main circuit fourbitorer
module fourbitorer (
  input  a3,
  input  b3,
  input  a2,
  input  b2,
  input  a1,
  input  b1,
  input  a0,
  input  b0,
  output OR3,
  output OR2,
  output OR1,
  output OR0
);

  or or_1 (OR3, a3, b3);
  or or_2 (OR2, a2, b2);
  or or_3 (OR1, a1, b1);
  or or_4 (OR0, a0, b0);
endmodule
