// Logisim project 4bitinverter.circ as structural Verilog: 1 circuit, main circuit fourbitinverter
module fourbitinverter (
  input  a3,
  input  a2,
  input  a1,
  input  a0,
  output a3out,
  output a2out,
  output a1out,
  output a0out
);

  not not_1 (a3out, a3);
  not not_2 (a2out, a2);
  not not_3 (a1out, a1);
  not not_4 (a0out, a0);
endmodule
