// Logisim project DualD.circ as structural Verilog: 1 circuit, main circuit main
module main (
  input  E,
  input  ck,
  input  reset,
  output outputz
);

  wire and_1_out, and_2_out, and_3_out, and_4_out, and_5_out, and_6_out, and_7_out, and_8_out, and_9_out,
       and_10_out, and_11_out, Da_q, Da_qn, Db_q, Db_qn, Dc_q, Dc_qn, not_1_out, not_2_out, or_2_out,
       or_3_out, or_4_out;

  not not_1 (not_1_out, E);
  and and_1 (and_1_out, not_1_out, Dc_qn, Db_qn, Da_qn);
  not not_2 (not_2_out, E);
  D_Flip_Flop Da (.D(or_4_out), .clk(ck), .Q(Da_q), .Qn(Da_qn), .preset(reset));  // open: reset
  D_Flip_Flop Db (.D(or_3_out), .clk(ck), .Q(Db_q), .Qn(Db_qn), .preset(reset));  // open: reset
  D_Flip_Flop Dc (.D(or_2_out), .clk(ck), .Q(Dc_q), .Qn(Dc_qn), .preset(reset));  // open: reset
  or or_1 (outputz, and_1_out, and_2_out);
  and and_2 (and_2_out, Dc_q, Da_q, Db_q);
  and and_3 (and_3_out, E, Dc_qn);
  and and_4 (and_4_out, Da_q, Db_q, not_2_out);
  or or_2 (or_2_out, and_4_out, and_6_out, and_3_out, and_9_out);
  and and_5 (and_5_out, Da_q, Db_qn);
  and and_6 (and_6_out, Da_q, Dc_qn);
  and and_7 (and_7_out, Db_qn, Dc_q);
  and and_8 (and_8_out, Da_qn, Db_q, Dc_q);
  and and_9 (and_9_out, Db_q, Dc_qn);
  and and_10 (and_10_out, Da_q, Dc_q, not_1_out);
  and and_11 (and_11_out, Db_q, Dc_q, not_1_out);
  or or_3 (or_3_out, and_9_out, and_7_out, and_10_out);
  or or_4 (or_4_out, and_5_out, and_8_out, and_11_out, and_6_out);
endmodule
