// Logisim project Lab1_Chips.circ as structural Verilog: 1 circuit, main circuit main
module main (
  input  B,
  input  D,
  input  C,
  output F
);

  wire n7404_1_pin8, n7408_1_pin3, n7408_1_pin11;

  _7404 #(.ShowInternalStructure("true")) u_7404_1 (
    .pin9(B), .pin8(n7404_1_pin8));  // open: pin1, pin2, pin3, pin4, pin5, pin6, pin13, pin12, pin11, pin10
  _7408 #(.ShowInternalStructure("true")) u_7408_1 (
    .pin1(D), .pin2(C), .pin3(n7408_1_pin3), .pin13(D), .pin12(n7404_1_pin8), .pin11(n7408_1_pin11));  // open: pin4, pin5, pin6, pin10, pin9, pin8
  _7432 #(.ShowInternalStructure("true")) u_7432_1 (
    .pin1(n7408_1_pin3), .pin2(n7408_1_pin11), .pin3(F));  // open: pin4, pin5, pin6, pin13, pin12, pin11, pin10, pin9, pin8
endmodule
