// Logisim project Lab1_Logic.circ as structural Verilog: 1 circuit, main circuit main
module main (
  input  B,
  input  D,
  input  C,
  output F
);

  wire A1_out, B1_out, C1_out;

  not A1 (A1_out, B);
  and B1 (B1_out, A1_out, D);
  and C1 (C1_out, D, C);
  or D1 (F, B1_out, C1_out);
endmodule
