// Logisim project lab1.circ as structural Verilog: 1 circuit, main circuit main
module main (
  input  A,
  input  B,
  input  C,
  output F
);

  wire A1_out, B1_out, C1_out, D1_out, n7400_1_pin2, n7400_1_pin3, n7400_1_pin4, n7400_1_pin5, n7400_1_pin6;

  not A1 (A1_out, B);
  _7404 #(.ShowInternalStructure("true")) u_7404_1 ();  // open: pin1, pin2, pin3, pin4, pin5, pin6, pin13, pin12, pin11, pin10, pin9, pin8
  _7400 #(.ShowInternalStructure("true")) u_7400_1 (
    .pin2(n7400_1_pin2), .pin3(n7400_1_pin3), .pin4(n7400_1_pin4), .pin5(n7400_1_pin5), .pin6(n7400_1_pin6));  // open: pin1, pin13, pin12, pin11, pin10, pin9, pin8
  _7402 #(.ShowInternalStructure("true")) u_7402_1 (
    .pin13(n7400_1_pin2), .pin12(n7400_1_pin3), .pin11(n7400_1_pin4), .pin10(n7400_1_pin5),
    .pin9(n7400_1_pin6));  // open: pin1, pin2, pin3, pin4, pin5, pin6, pin8
  and B1 (B1_out, A, A1_out);
  and C1 (C1_out, B, C);
  xor D1 (D1_out, B1_out, C1_out);
  _7408 #(.ShowInternalStructure("true")) u_7408_1 ();  // open: pin1, pin2, pin3, pin4, pin5, pin6, pin13, pin12, pin11, pin10, pin9, pin8
  _7410 #(.ShowInternalStructure("true")) u_7410_1 ();  // open: pin1, pin2, pin3, pin4, pin5, pin6, pin13, pin12, pin11, pin10, pin9, pin8
  _7411 #(.ShowInternalStructure("true")) u_7411_1 ();  // open: pin1, pin2, pin3, pin4, pin5, pin6, pin13, pin12, pin11, pin10, pin9, pin8
  not E1 (F, D1_out);
endmodule
