// Logisim project labpt1.circ as structural Verilog: 1 circuit, main circuit main
module main (
  input  c1,
  input  c0,
  input  r,
  output A,
  output m1,
  output m0
);

  wire nand_1_out, nand_2_out, nand_3_out, nand_4_out, nand_5_out, nand_6_out, nand_8_out, not_1_out,
       not_2_out, not_3_out, not_4_out, not_5_out, not_6_out, not_8_out;

  not not_1 (not_1_out, c1);
  not not_2 (not_2_out, c0);
  not not_3 (not_3_out, r);
  not not_4 (not_4_out, r);
  nand nand_1 (nand_1_out, c1, c0);
  nand nand_2 (nand_2_out, not_1_out, not_2_out);
  not not_5 (not_5_out, c0);
  nand nand_3 (nand_3_out, c0, not_3_out);
  nand nand_4 (nand_4_out, c1, not_4_out);
  not not_6 (not_6_out, nand_2_out);
  nand nand_5 (nand_5_out, r, not_5_out);
  nand nand_6 (nand_6_out, not_6_out, r);
  nand nand_7 (m0, nand_5_out, nand_3_out);
  not not_7 (A, nand_6_out);
  nand nand_8 (nand_8_out, nand_1_out, nand_6_out);
  not not_8 (not_8_out, nand_8_out);
  nand nand_9 (m1, not_8_out, nand_4_out);
endmodule
