// Logisim project labpt2.circ as structural Verilog: 1 circuit, main circuit main
module main (
  input  h,
  input  i,
  input  j,
  input  k,
  output f1
);

  wire nor_1_out, nor_2_out, nor_3_out, not_1_out, not_2_out;

  nor nor_1 (nor_1_out, h, k);
  not not_1 (not_1_out, k);
  nor nor_2 (nor_2_out, i, not_1_out);
  nor nor_3 (nor_3_out, nor_1_out, nor_2_out);
  not not_2 (not_2_out, nor_3_out);
  nor nor_4 (f1, not_2_out, j);
endmodule
