// Logisim project vcsc.circ as structural Verilog: 1 circuit, main circuit main
module main (
  input  RA,
  input  [3:0] in_2,
  input  z,
  input  addr,
  input  RB,
  input  IR,
  input  y,
  input  x,
  input  [2:0] in_9,
  input  in_10,
  input  in_11,
  input  in_12,
  output out_13,
  output [3:0] out_14
);

  wire and_1_out, and_2_out, and_3_out, controlled_buffer_1_out, controlled_buffer_2_out,
       controlled_buffer_3_out, controlled_buffer_6_out, controlled_buffer_7_out, Memory0_q, Memory1_q,
       not_1_out, not_2_out, not_3_out, not_4_out, undriven;
  wire [2:0] Instruction_q;
  wire [3:0] RegisterA_q, RegisterB_q;

  Register #(.width(3)) Instruction (.D(in_9), .en(controlled_buffer_3_out), .clk(x), .Q(Instruction_q), .clr(in_11));
  not not_1 (not_1_out, Instruction_q[2]);
  not not_2 (not_2_out, Instruction_q[1]);
  not not_3 (not_3_out, Instruction_q[0]);
  and and_1 (and_1_out, y, not_1_out);
  Register #(.width(4)) RegisterA (.D(in_2), .en(undriven), .clk(and_1_out), .Q(RegisterA_q), .clr(and_2_out));
  and and_2 (and_2_out, Instruction_q[2], not_2_out, not_3_out);
  and and_3 (and_3_out, z, not_1_out);
  Register #(.width(4)) RegisterB (
    .D(out_14), .en(controlled_buffer_1_out), .clk(and_3_out), .Q(RegisterB_q), .clr(and_2_out));
  fourbit_alu fourbit_alu_1 (
    .A(RegisterA_q), .B(RegisterB_q), .S(Instruction_q[1:0]), .carry(out_13), .alu3(out_14[3]),
    .alu2(out_14[2]), .alu1(out_14[1]), .alu0(out_14[0]));
  assign controlled_buffer_1_out = RB ? controlled_buffer_2_out : 1'bz;  // Controlled_Buffer controlled_buffer_1
  assign controlled_buffer_2_out = RA ? undriven : 1'bz;  // Controlled_Buffer controlled_buffer_2
  assign controlled_buffer_3_out = IR ? controlled_buffer_2_out : 1'bz;  // Controlled_Buffer controlled_buffer_3
  not not_4 (not_4_out, addr);
  assign controlled_buffer_2_out = addr ? Memory1_q : 1'bz;  // Controlled_Buffer controlled_buffer_4
  assign controlled_buffer_2_out = not_4_out ? Memory0_q : 1'bz;  // Controlled_Buffer controlled_buffer_5
  assign controlled_buffer_6_out = addr ? controlled_buffer_2_out : 1'bz;  // Controlled_Buffer controlled_buffer_6
  assign controlled_buffer_7_out = not_4_out ? controlled_buffer_2_out : 1'bz;  // Controlled_Buffer controlled_buffer_7
  Register #(.width(1)) Memory1 (.D(controlled_buffer_6_out), .en(in_10), .Q(Memory1_q));  // open: clk, clr
  Register #(.width(1)) Memory0 (.D(controlled_buffer_7_out), .en(in_12), .Q(Memory0_q));  // open: clk, clr
endmodule
