// Logisim project 4bit_alu_sample.circ as structural Verilog: 1 circuit, main circuit fourbit_alu
module fourbit_alu (
  input  [3:0] A,
  input  [3:0] B,
  input  [1:0] S,
  output carry,
  output alu3,
  output alu2,
  output alu1,
  output alu0
);

  wire fourbit_adder_1_sum0, fourbit_adder_1_sum1, fourbit_adder_1_sum2, fourbit_adder_1_sum3,
       fourbitander_1_and0, fourbitander_1_and1, fourbitander_1_and2, fourbitander_1_and3,
       fourbitinverter_1_a0out, fourbitinverter_1_a1out, fourbitinverter_1_a2out, fourbitinverter_1_a3out,
       fourbitorer_1_or0, fourbitorer_1_or1, fourbitorer_1_or2, fourbitorer_1_or3;

  fourbit_adder fourbit_adder_1 (
    .A1(A[1]), .B1(B[1]), .A0(A[0]), .B0(B[0]), .A2(A[2]), .B2(B[2]), .A3(A[3]), .B3(B[3]), .Carry(carry),
    .Sum3(fourbit_adder_1_sum3), .Sum1(fourbit_adder_1_sum1), .Sum0(fourbit_adder_1_sum0),
    .Sum2(fourbit_adder_1_sum2));
  fourbitander fourbitander_1 (
    .a3(A[3]), .b3(B[3]), .a2(A[2]), .b2(B[2]), .a1(A[1]), .b1(B[1]), .a0(A[0]), .b0(B[0]),
    .and3(fourbitander_1_and3), .and2(fourbitander_1_and2), .and1(fourbitander_1_and1),
    .and0(fourbitander_1_and0));
  fourbitorer fourbitorer_1 (
    .a3(A[3]), .b3(B[3]), .a2(A[2]), .b2(B[2]), .a1(A[1]), .b1(B[1]), .a0(A[0]), .b0(B[0]),
    .OR3(fourbitorer_1_or3), .OR2(fourbitorer_1_or2), .OR1(fourbitorer_1_or1), .OR0(fourbitorer_1_or0));
  fourbitinverter fourbitinverter_1 (
    .a3(A[3]), .a2(A[2]), .a1(A[1]), .a0(A[0]), .a3out(fourbitinverter_1_a3out),
    .a2out(fourbitinverter_1_a2out), .a1out(fourbitinverter_1_a1out), .a0out(fourbitinverter_1_a0out));
  Multiplexer #(.select(2)) multiplexer_1 (
    .in0(fourbitinverter_1_a3out), .in1(fourbitorer_1_or3), .in2(fourbitander_1_and3),
    .in3(fourbit_adder_1_sum3), .out(alu3), .sel(S));
  Multiplexer #(.select(2)) multiplexer_2 (
    .in0(fourbitinverter_1_a2out), .in1(fourbitorer_1_or2), .in2(fourbitander_1_and2),
    .in3(fourbit_adder_1_sum2), .out(alu2), .sel(S));
  Multiplexer #(.select(2)) multiplexer_3 (
    .in0(fourbitinverter_1_a1out), .in1(fourbitorer_1_or1), .in2(fourbitander_1_and1),
    .in3(fourbit_adder_1_sum1), .out(alu1), .sel(S));
  Multiplexer #(.select(2)) multiplexer_4 (
    .in0(fourbitinverter_1_a0out), .in1(fourbitorer_1_or0), .in2(fourbitander_1_and0),
    .in3(fourbit_adder_1_sum0), .out(alu0), .sel(S));
endmodule
