// Logisim project 4bitadder.circ as structural Verilog: 3 circuits, main circuit fourbit_adder
module fourbit_adder (
  input  A1,
  input  B1,
  input  A0,
  input  B0,
  input  A2,
  input  B2,
  input  A3,
  input  B3,
  output Carry,
  output Sum3,
  output Sum1,
  output Sum0,
  output Sum2
);

  wire full_adder_2_cout, full_adder_3_cout, half_adder_1_cout;

  full_adder full_adder_1 (.A(A3), .B(B3), .Cin(full_adder_2_cout), .S(Sum3), .Cout(Carry));
  full_adder full_adder_2 (.A(A2), .B(B2), .Cin(full_adder_3_cout), .S(Sum2), .Cout(full_adder_2_cout));
  full_adder full_adder_3 (.A(A1), .B(B1), .Cin(half_adder_1_cout), .S(Sum1), .Cout(full_adder_3_cout));
  half_adder half_adder_1 (.X(A0), .Y(B0), .S(Sum0), .cout(half_adder_1_cout));
endmodule

module half_adder (
  input  X,
  input  Y,
  output S,
  output cout
);

  xor xor_1 (S, X, Y);
  and and_1 (cout, Y, X);
endmodule

module full_adder (
  input  A,
  input  B,
  input  Cin,
  output S,
  output Cout
);

  wire half_adder_1_cout, half_adder_1_s, half_adder_2_cout;

  half_adder half_adder_1 (.X(A), .Y(B), .S(half_adder_1_s), .cout(half_adder_1_cout));
  half_adder half_adder_2 (.X(half_adder_1_s), .Y(Cin), .S(S), .cout(half_adder_2_cout));
  or or_1 (Cout, half_adder_2_cout, half_adder_1_cout);
endmodule
