// Logisim project busses_4bitadder.circ as structural Verilog: 1 circuit, main circuit main
module main (
  input  [3:0] A,
  input  [3:0] B,
  output out_3,
  output [3:0] F
);

  fourbit_adder fourbit_adder_1 (
    .A1(A[1]), .B1(B[1]), .A0(A[0]), .B0(B[0]), .A2(A[2]), .B2(B[2]), .A3(A[3]), .B3(B[3]), .Carry(out_3),
    .Sum3(F[3]), .Sum1(F[1]), .Sum0(F[0]), .Sum2(F[2]));
endmodule
