// Logisim project lab2pt3.circ as structural Verilog: 1 circuit, main circuit main
module main (
  input  i1,
  input  h1,
  input  k1,
  input  j1,
  output f2
);

  wire n7402_1_pin1, n7402_1_pin2, n7402_1_pin4, n7402_1_pin9, n7402_1_pin13;

  _7402 #(.ShowInternalStructure("true")) u_7402_1 (
    .pin1(n7402_1_pin1), .pin2(n7402_1_pin2), .pin3(i1), .pin4(n7402_1_pin4), .pin5(k1), .pin6(h1),
    .pin13(n7402_1_pin13), .pin12(n7402_1_pin4), .pin11(n7402_1_pin1), .pin10(f2), .pin9(n7402_1_pin9),
    .pin8(j1));
  _7404 #(.ShowInternalStructure("true")) u_7404_1 (
    .pin1(k1), .pin2(n7402_1_pin2), .pin9(n7402_1_pin13), .pin8(n7402_1_pin9));  // open: pin3, pin4, pin5, pin6, pin13, pin12, pin11, pin10
endmodule
