// Logisim project lab53bc.circ as structural Verilog: 1 circuit, main circuit main
module main (
  input  MR,
  input  PLprime,
  input  countup,
  input  countdown,
  input  LT,
  input  RBO,
  input  RBI,
  input  b,
  input  c,
  input  d,
  input  a
);

  wire n7447_1_pin9, n7447_1_pin10, n7447_1_pin11, n7447_1_pin12, n7447_1_pin13, n7447_1_pin14,
       n7447_1_pin15, n7447_2_pin9, n7447_2_pin10, n7447_2_pin11, n7447_2_pin12, n7447_2_pin13,
       n7447_2_pin14, n7447_2_pin15, n74192_1_pin2, n74192_1_pin3, n74192_1_pin6, n74192_1_pin7;

  _74192 #(.ShowInternalStructure("true")) u_74192_1 (
    .pin2(n74192_1_pin2), .pin3(n74192_1_pin3), .pin4(countdown), .pin5(countup), .pin6(n74192_1_pin6),
    .pin7(n74192_1_pin7), .pin14(MR), .pin11(PLprime));  // open: pin1, pin15, pin13, pin12, pin10, pin9
  LED #(.active("false")) led_1 (.in(n7447_1_pin15));
  _7447 #(.ShowInternalStructure("true")) u_7447_1 (
    .pin1(b), .pin2(c), .pin6(d), .pin7(a), .pin15(n7447_1_pin15), .pin14(n7447_1_pin14),
    .pin13(n7447_1_pin13), .pin12(n7447_1_pin12), .pin11(n7447_1_pin11), .pin10(n7447_1_pin10),
    .pin9(n7447_1_pin9));  // open: pin3, pin4, pin5
  LED #(.active("false")) led_2 (.in(n7447_1_pin14));
  LED #(.active("false")) led_3 (.in(n7447_1_pin13));
  LED #(.active("false")) led_4 (.in(n7447_1_pin12));
  LED #(.active("false")) led_5 (.in(n7447_1_pin11));
  LED #(.active("false")) led_6 (.in(n7447_1_pin10));
  LED #(.active("false")) led_7 (.in(n7447_1_pin9));
  _7447 #(.ShowInternalStructure("true")) u_7447_2 (
    .pin1(n74192_1_pin2), .pin2(n74192_1_pin6), .pin3(LT), .pin4(RBI), .pin5(RBO), .pin6(n74192_1_pin7),
    .pin7(n74192_1_pin3), .pin15(n7447_2_pin15), .pin14(n7447_2_pin14), .pin13(n7447_2_pin13),
    .pin12(n7447_2_pin12), .pin11(n7447_2_pin11), .pin10(n7447_2_pin10), .pin9(n7447_2_pin9));
  _7_Segment_Display #(.active("false")) u_7_segment_display_1 (
    .g(n7447_2_pin14), .f(n7447_2_pin15), .a(n7447_2_pin13), .b(n7447_2_pin12), .e(n7447_2_pin9),
    .d(n7447_2_pin10), .c(n7447_2_pin11));  // open: dp
endmodule
